// Logisim project P M C comp multicor.circ as structural Verilog: 7 circuits, main circuit main
module main (
);

  wire button_1_out, button_3_out, button_4_out, button_5_out, button_6_out, button_7_out, button_8_out, CLK,
       clock_1_out, Clr, controlled_buffer_1_out, multiplexer_3_out, multiplexer_4_out, multiplexer_5_out,
       nor_1_out, not_1_out, not_2_out, proc_1_mem2reg_2, proc_1_memwrite, proc_1_reg2screen,
       proc_2_mem2reg_2, proc_2_memwrite, proc_2_reg2screen;
  wire [15:0] multiplexer_1_out, proc_1_memadr, proc_1_pc_val, proc_2_memadr, proc_2_pc_val;
  wire [31:0] display_1_col_2, display_1_row_2, inputcontrol_1_out, multiplexer_2_out, multiplexer_6_out,
       multiplexer_7_out, proc_1_rs, proc_1_rt, proc_2_rs, proc_2_rt, ram_1_data, rom_1_data, rom_2_data;

  or or_1 (CLK, clock_1_out, button_1_out);
  Button button_1 (.out(button_1_out));
  Clock clock_1 (.out(clock_1_out));
  ROM #(.addrWidth(16), .dataWidth(32)) rom_1 (.addr(proc_1_pc_val), .data(rom_1_data));  // open: sel
  Button button_2 (.out(Clr));
  Button button_3 (.out(button_3_out));
  Button button_4 (.out(button_4_out));
  Button button_5 (.out(button_5_out));
  ROM #(.addrWidth(16), .dataWidth(32)) rom_2 (.addr(proc_2_pc_val), .data(rom_2_data));  // open: sel
  assign controlled_buffer_1_out = nor_1_out ? CLK : 1'bz;  // Controlled_Buffer controlled_buffer_1
  Proc proc_1 (
    .Instr(rom_1_data), .Mem2reg(ram_1_data), .reg2screen(proc_1_reg2screen), .memwrite(proc_1_memwrite),
    .PC_val(proc_1_pc_val), .RS(proc_1_rs), .MemAdr(proc_1_memadr), .RT(proc_1_rt), .CLK(CLK), .clr(Clr),
    .Input(inputcontrol_1_out), .mem2reg_2(proc_1_mem2reg_2));
  Button button_6 (.out(button_6_out));
  InputControl inputcontrol_1 (
    .U(button_3_out), .D(button_5_out), .R(button_8_out), .L(button_4_out), .Out(inputcontrol_1_out),
    .B1(button_6_out), .B2(button_7_out));
  Button button_7 (.out(button_7_out));
  Button button_8 (.out(button_8_out));
  Proc proc_2 (
    .Instr(rom_2_data), .Mem2reg(ram_1_data), .reg2screen(proc_2_reg2screen), .memwrite(proc_2_memwrite),
    .PC_val(proc_2_pc_val), .RS(proc_2_rs), .MemAdr(proc_2_memadr), .RT(proc_2_rt),
    .CLK(controlled_buffer_1_out), .clr(Clr), .mem2reg_2(proc_2_mem2reg_2));  // open: Input
  nor nor_1 (nor_1_out, proc_1_mem2reg_2, proc_1_memwrite);
  Multiplexer #(.width(16), .enable("false")) multiplexer_1 (
    .in0(proc_1_memadr), .in1(proc_2_memadr), .out(multiplexer_1_out), .sel(nor_1_out));
  Multiplexer #(.width(32), .enable("false")) multiplexer_2 (
    .in0(proc_1_rt), .in1(proc_2_rt), .out(multiplexer_2_out), .sel(nor_1_out));
  Multiplexer #(.enable("false")) multiplexer_3 (
    .in0(proc_1_reg2screen), .in1(proc_2_reg2screen), .out(multiplexer_3_out), .sel(not_1_out));
  not not_1 (not_1_out, proc_1_reg2screen);
  Multiplexer #(.enable("false")) multiplexer_4 (
    .in0(proc_1_mem2reg_2), .in1(proc_2_mem2reg_2), .out(multiplexer_4_out), .sel(nor_1_out));
  Multiplexer #(.enable("false")) multiplexer_5 (
    .in0(proc_1_memwrite), .in1(proc_2_memwrite), .out(multiplexer_5_out), .sel(nor_1_out));
  Multiplexer #(.width(32), .enable("false")) multiplexer_6 (
    .in0(proc_1_rs), .in1(proc_2_rs), .out(multiplexer_6_out), .sel(not_1_out));
  Multiplexer #(.width(32), .enable("false")) multiplexer_7 (
    .in0(proc_1_rt), .in1(proc_2_rt), .out(multiplexer_7_out), .sel(not_1_out));
  not not_2 (not_2_out, CLK);
  Display display_1 (
    .Col(multiplexer_6_out), .Col_2(display_1_col_2), .Row_2(display_1_row_2), .CLK(CLK),
    .Enable(multiplexer_3_out), .Clr(Clr), .Row(multiplexer_7_out));
  // DotMatrix #(.inputtype("select"), .matrixcols(32), .matrixrows(32), .persist(200)) dotmatrix_1: pin names not known; wires that end beside it: display_1_col_2, display_1_row_2
  RAM #(.addrWidth(16), .dataWidth(32), .bus("separate")) ram_1 (
    .addr(multiplexer_1_out), .din(multiplexer_2_out), .data(ram_1_data), .str(multiplexer_5_out),
    .clk(not_2_out), .ld(multiplexer_4_out), .clr(Clr));  // open: sel

  // Notes on the sheet:
  //   contents of rom_1 (hex, n*v repeats v):
  //   0 21000001 22000001 23000001 24004000 64408000 64400004 27000001 2f000000 d0230000 28000000 a08f0005
  //   b9800000 ba800001 d09a0000 28800002 9000fffa e5000000 a050fff6 a0340004 26000001 a0560001 90000001
  //   63300002 a0310004 26000002 a0560001 90000001 83300002 a0240004 26000004 a0560001 90000001 62200002
  //   a0210004 26000008 a0560001 90000001 82200002 a070000b 26000010 a0560001 90000003 c0f20000 c0f30001
  //   2ff00002 a0f00004 26000020 a0560001 90000001 2ff0fffe 26000010 a0560004 26000020 a0560002 27000001
  //   90000001 27000000 9000ffce
  //   contents of rom_2 (hex, n*v repeats v):
  //   0 21000001 22000001 23000001 24004000 64408000 64400004 27000001 2f000000 d0230000 28000000 a08f0005
  //   b9800000 ba800001 d09a0000 28800002 9000fffa e5000000 a050fff6 a0340004 26000001 a0560001 90000001
  //   63300002 a0310004 26000002 a0560001 90000001 83300002 a0240004 26000004 a0560001 90000001 62200002
  //   a0210004 26000008 a0560001 90000001 82200002 a070000b 26000010 a0560001 90000003 c0f20000 c0f30001
  //   2ff00002 a0f00004 26000020 a0560001 90000001 2ff0fffe 26000010 a0560004 26000020 a0560002 27000001
  //   90000001 27000000 9000ffce
endmodule

module Proc (
  input  [31:0] Instr,
  input  [31:0] Mem2reg,
  input  [31:0] Input,
  input  CLK,
  input  clr,
  output reg2screen,
  output mem2reg_2,
  output memwrite,
  output [15:0] PC_val,
  output [31:0] RS,
  output [15:0] MemAdr,
  output [31:0] RT
);

  wire and_1_out, not_1_out, or_1_out, uc4_1_branch, uc4_1_inp2reg, uc4_1_jump, uc4_1_regwrite,
       uc4_1_ula_src, ula_1_comp_eq;
  wire [1:0] uc4_1_ula_op;
  wire [15:0] adder_1_out, adder_2_out, multiplexer_3_out;
  wire [31:0] bit_extender_1_out, multiplexer_1_out, multiplexer_2_out, multiplexer_4_out, ula_1_ula_out;

  Register #(.width(16)) register_1 (.D(multiplexer_3_out), .Q(PC_val), .clk(CLK), .clr(clr));  // open: en
  Adder #(.width(16)) adder_1 (.a(16'h1), .b(PC_val), .out(adder_1_out));  // open: cin, cout
  Adder #(.width(16)) adder_2 (.a(adder_1_out), .b(Instr[15:0]), .out(adder_2_out));  // open: cin, cout
  UC4 uc4_1 (
    .Input(Instr[31:28]), .ULA_Op(uc4_1_ula_op), .ula_src(uc4_1_ula_src), .jump(uc4_1_jump),
    .branch(uc4_1_branch), .mem2reg(mem2reg_2), .memwrite(memwrite), .regwrite(uc4_1_regwrite),
    .reg2screen(reg2screen), .inp2reg(uc4_1_inp2reg));
  not not_1 (not_1_out, CLK);
  Multiplexer #(.width(32), .enable("false")) multiplexer_1 (
    .in0(multiplexer_4_out), .in1(Input), .out(multiplexer_1_out), .sel(uc4_1_inp2reg));
  Bank_Regis bank_regis_1 (
    .Clear(clr), .RD(Instr[27:24]), .WriteValue(multiplexer_1_out), .Write(uc4_1_regwrite),
    .RS(Instr[23:20]), .RT(Instr[19:16]), .RS_Out(RS), .RT_Out(RT), .CLK(not_1_out));
  assign bit_extender_1_out = {{16{Instr[15]}}, Instr[15:0]};  // Bit_Extender bit_extender_1
  Multiplexer #(.width(32), .enable("false")) multiplexer_2 (
    .in0(RT), .in1(bit_extender_1_out), .out(multiplexer_2_out), .sel(uc4_1_ula_src));
  Multiplexer #(.width(16), .enable("false")) multiplexer_3 (
    .in0(adder_1_out), .in1(adder_2_out), .out(multiplexer_3_out), .sel(or_1_out));
  or or_1 (or_1_out, uc4_1_jump, and_1_out);
  and and_1 (and_1_out, uc4_1_branch, ula_1_comp_eq);
  ULA ula_1 (.RS(RS), .RT(multiplexer_2_out), .ULA_Out(ula_1_ula_out), .Comp_EQ(ula_1_comp_eq), .OP(uc4_1_ula_op));
  Bit_Extender #(.in_width(32), .\type ("sign")) bit_extender_2 (.in(ula_1_ula_out), .out(MemAdr));
  Multiplexer #(.width(32), .enable("false")) multiplexer_4 (
    .in0(ula_1_ula_out), .in1(Mem2reg), .out(multiplexer_4_out), .sel(mem2reg_2));
endmodule

module Bank_Regis (
  input  Write,
  input  [3:0] RD,
  input  [3:0] RS,
  input  [3:0] RT,
  input  [31:0] WriteValue,
  input  CLK,
  input  Clear,
  output [31:0] RS_Out,
  output [31:0] RT_Out
);

  wire demultiplexer_1_out0, demultiplexer_1_out1, demultiplexer_1_out2, demultiplexer_1_out3,
       demultiplexer_1_out4, demultiplexer_1_out5, demultiplexer_1_out6, demultiplexer_1_out7,
       demultiplexer_1_out8, demultiplexer_1_out9, demultiplexer_1_out10, demultiplexer_1_out11,
       demultiplexer_1_out12, demultiplexer_1_out13, demultiplexer_1_out14, demultiplexer_1_out15;
  wire [31:0] register_1_q, register_2_q, register_3_q, register_4_q, register_5_q, register_6_q,
       register_7_q, register_8_q, register_9_q, register_10_q, register_11_q, register_12_q, register_13_q,
       register_14_q, register_15_q, register_16_q;

  Demultiplexer #(.select(4), .enable("false")) demultiplexer_1 (
    .out0(demultiplexer_1_out0), .out1(demultiplexer_1_out1), .out2(demultiplexer_1_out2),
    .out3(demultiplexer_1_out3), .out4(demultiplexer_1_out4), .out5(demultiplexer_1_out5),
    .out6(demultiplexer_1_out6), .out7(demultiplexer_1_out7), .out8(demultiplexer_1_out8),
    .out9(demultiplexer_1_out9), .out10(demultiplexer_1_out10), .out11(demultiplexer_1_out11),
    .out12(demultiplexer_1_out12), .out13(demultiplexer_1_out13), .out14(demultiplexer_1_out14),
    .out15(demultiplexer_1_out15), .in(Write), .sel(RD));
  Register #(.width(32)) register_1 (
    .D(WriteValue), .en(demultiplexer_1_out0), .Q(register_1_q), .clk(CLK), .clr(Clear));
  Register #(.width(32)) register_2 (
    .D(WriteValue), .en(demultiplexer_1_out1), .Q(register_2_q), .clk(CLK), .clr(Clear));
  Register #(.width(32)) register_3 (
    .D(WriteValue), .en(demultiplexer_1_out2), .Q(register_3_q), .clk(CLK), .clr(Clear));
  Register #(.width(32)) register_4 (
    .D(WriteValue), .en(demultiplexer_1_out3), .Q(register_4_q), .clk(CLK), .clr(Clear));
  Register #(.width(32)) register_5 (
    .D(WriteValue), .en(demultiplexer_1_out4), .Q(register_5_q), .clk(CLK), .clr(Clear));
  Register #(.width(32)) register_6 (
    .D(WriteValue), .en(demultiplexer_1_out5), .Q(register_6_q), .clk(CLK), .clr(Clear));
  Register #(.width(32)) register_7 (
    .D(WriteValue), .en(demultiplexer_1_out6), .Q(register_7_q), .clk(CLK), .clr(Clear));
  Register #(.width(32)) register_8 (
    .D(WriteValue), .en(demultiplexer_1_out7), .Q(register_8_q), .clk(CLK), .clr(Clear));
  Register #(.width(32)) register_9 (
    .D(WriteValue), .en(demultiplexer_1_out8), .Q(register_9_q), .clk(CLK), .clr(Clear));
  Register #(.width(32)) register_10 (
    .D(WriteValue), .en(demultiplexer_1_out9), .Q(register_10_q), .clk(CLK), .clr(Clear));
  Register #(.width(32)) register_11 (
    .D(WriteValue), .en(demultiplexer_1_out10), .Q(register_11_q), .clk(CLK), .clr(Clear));
  Register #(.width(32)) register_12 (
    .D(WriteValue), .en(demultiplexer_1_out11), .Q(register_12_q), .clk(CLK), .clr(Clear));
  Register #(.width(32)) register_13 (
    .D(WriteValue), .en(demultiplexer_1_out12), .Q(register_13_q), .clk(CLK), .clr(Clear));
  Register #(.width(32)) register_14 (
    .D(WriteValue), .en(demultiplexer_1_out13), .Q(register_14_q), .clk(CLK), .clr(Clear));
  Register #(.width(32)) register_15 (
    .D(WriteValue), .en(demultiplexer_1_out14), .Q(register_15_q), .clk(CLK), .clr(Clear));
  Register #(.width(32)) register_16 (
    .D(WriteValue), .en(demultiplexer_1_out15), .Q(register_16_q), .clk(CLK), .clr(Clear));
  Multiplexer #(.select(4), .width(32), .enable("false")) multiplexer_1 (
    .in0(register_1_q), .in1(register_2_q), .in2(register_3_q), .in3(register_4_q), .in4(register_5_q),
    .in5(register_6_q), .in6(register_7_q), .in7(register_8_q), .in8(register_9_q), .in9(register_10_q),
    .in10(register_11_q), .in11(register_12_q), .in12(register_13_q), .in13(register_14_q),
    .in14(register_15_q), .in15(register_16_q), .out(RS_Out), .sel(RS));
  Multiplexer #(.select(4), .width(32), .enable("false")) multiplexer_2 (
    .in0(register_1_q), .in1(register_2_q), .in2(register_3_q), .in3(register_4_q), .in4(register_5_q),
    .in5(register_6_q), .in6(register_7_q), .in7(register_8_q), .in8(register_9_q), .in9(register_10_q),
    .in10(register_11_q), .in11(register_12_q), .in12(register_13_q), .in13(register_14_q),
    .in14(register_15_q), .in15(register_16_q), .out(RT_Out), .sel(RT));

  // Other names for the same wires on the sheet: Clr = Clear
endmodule

module ULA (
  input  [31:0] RS,
  input  [1:0] OP,
  input  [31:0] RT,
  output [31:0] ULA_Out,
  output Comp_EQ
);

  wire [31:0] adder_1_out, divider_1_out, multiplier_1_out, subtractor_1_out;

  Adder #(.width(32)) adder_1 (.a(RS), .b(RT), .out(adder_1_out));  // open: cin, cout
  Subtractor #(.width(32)) subtractor_1 (.a(RS), .b(RT), .out(subtractor_1_out));  // open: bin, bout
  Multiplier #(.width(32)) multiplier_1 (.a(RS), .b(RT), .out(multiplier_1_out));  // open: cin, cout
  Divider #(.width(32)) divider_1 (.a(RS), .b(RT), .out(divider_1_out));  // open: upper, rem
  Comparator #(.width(32)) comparator_1 (.a(RS), .b(RT), .eq(Comp_EQ));  // open: gt, lt
  Multiplexer #(.select(2), .width(32), .enable("false")) multiplexer_1 (
    .in0(adder_1_out), .in1(subtractor_1_out), .in2(multiplier_1_out), .in3(divider_1_out), .out(ULA_Out),
    .sel(OP));
endmodule

module UC4 (
  input  [3:0] Input,
  output [1:0] ULA_Op,
  output ula_src,
  output jump,
  output branch,
  output mem2reg,
  output memwrite,
  output regwrite,
  output reg2screen,
  output inp2reg
);

  wire and_4_out, and_5_out, and_6_out, and_7_out, and_8_out, and_9_out, and_10_out, and_11_out, and_12_out,
       and_16_out, and_17_out, and_18_out, and_19_out, and_20_out, and_21_out, not_1_out, not_2_out,
       not_3_out, not_4_out, not_5_out, not_6_out, not_7_out, not_8_out, not_9_out, not_10_out, not_11_out,
       not_12_out, not_13_out, not_14_out, not_15_out, not_16_out, not_17_out, not_18_out, not_19_out,
       not_20_out, not_21_out, not_22_out, not_23_out, not_24_out, not_25_out, not_26_out;

  not not_1 (not_1_out, Input[2]);
  not not_2 (not_2_out, Input[1]);
  not not_3 (not_3_out, Input[0]);
  not not_4 (not_4_out, Input[3]);
  not not_5 (not_5_out, Input[1]);
  not not_6 (not_6_out, Input[0]);
  not not_7 (not_7_out, Input[2]);
  not not_8 (not_8_out, Input[1]);
  not not_9 (not_9_out, Input[0]);
  not not_10 (not_10_out, Input[3]);
  not not_11 (not_11_out, Input[3]);
  not not_12 (not_12_out, Input[0]);
  not not_13 (not_13_out, Input[1]);
  not not_14 (not_14_out, Input[0]);
  not not_15 (not_15_out, Input[2]);
  not not_16 (not_16_out, Input[1]);
  not not_17 (not_17_out, Input[2]);
  not not_18 (not_18_out, Input[0]);
  and and_1 (mem2reg, Input[3], Input[1]);
  not not_19 (not_19_out, Input[1]);
  not not_20 (not_20_out, Input[0]);
  not not_21 (not_21_out, Input[3]);
  not not_22 (not_22_out, Input[3]);
  not not_23 (not_23_out, Input[3]);
  not not_24 (not_24_out, Input[2]);
  not not_25 (not_25_out, Input[1]);
  not not_26 (not_26_out, Input[0]);
  and and_2 (reg2screen, Input[3], Input[2], Input[0]);
  and and_3 (inp2reg, Input[3], Input[2]);
  and and_4 (and_4_out, not_1_out, not_2_out, not_3_out);
  or or_1 (ULA_Op[1], and_4_out, and_5_out, and_6_out);
  and and_5 (and_5_out, Input[2], Input[0]);
  and and_6 (and_6_out, Input[2], Input[1]);
  and and_7 (and_7_out, not_4_out, not_5_out, not_6_out);
  or or_2 (ULA_Op[0], and_7_out, and_8_out, and_9_out);
  and and_8 (and_8_out, not_7_out, not_8_out, not_9_out);
  and and_9 (and_9_out, not_10_out, Input[1], Input[0]);
  and and_10 (and_10_out, not_11_out, not_12_out);
  and and_11 (and_11_out, not_13_out, not_14_out);
  or or_3 (ula_src, and_10_out, and_11_out, and_12_out);
  and and_12 (and_12_out, Input[3], Input[0]);
  and and_13 (jump, Input[3], not_15_out, not_16_out, Input[0]);
  and and_14 (branch, Input[3], not_17_out, Input[1], not_18_out);
  and and_15 (memwrite, Input[3], Input[2], not_19_out, not_20_out);
  and and_16 (and_16_out, not_21_out, Input[0]);
  and and_17 (and_17_out, not_22_out, Input[1]);
  and and_18 (and_18_out, Input[1], Input[0]);
  and and_19 (and_19_out, not_23_out, Input[2]);
  and and_20 (and_20_out, Input[2], Input[1]);
  and and_21 (and_21_out, Input[3], not_24_out, not_25_out, not_26_out);
  or or_4 (regwrite, and_16_out, and_17_out, and_18_out, and_19_out, and_20_out, and_21_out);
endmodule

module Display (
  input  Enable,
  input  [31:0] Col,
  input  [31:0] Row,
  input  CLK,
  input  Clr,
  output [31:0] Col_2,
  output [31:0] Row_2
);

  Register #(.width(32)) register_1 (.D(Col), .en(Enable), .Q(Col_2), .clk(CLK), .clr(Clr));
  Register #(.width(32)) register_2 (.D(Row), .en(Enable), .Q(Row_2), .clk(CLK), .clr(Clr));
endmodule

module InputControl (
  input  U,
  input  D,
  input  R,
  input  L,
  input  B1,
  input  B2,
  output [31:0] Out
);

  assign Out = {{26{1'b0}}, {B2, B1, L, R, D, U}};  // Bit_Extender bit_extender_1
endmodule
