// Logisim project Processador Mips Custom.circ as structural Verilog: 5 circuits, main circuit main
module main (
  input  in_1
);

  wire and_1_out, button_1_out, CLK, clock_1_out, Clr, not_1_out, not_2_out, or_2_out, uc_1_branch,
       uc_1_jump, uc_1_mem2reg, uc_1_memwrite, uc_1_regwrite, uc_1_ula_src, ula_1_comp_eq;
  wire [1:0] uc_1_regsrc, uc_1_ula_op;
  wire [15:0] adder_1_out, adder_2_out, bit_extender_2_out, multiplexer_3_out, register_1_q;
  wire [31:0] bank_regis_1_rs_out, bank_regis_1_rt_out, bit_extender_1_out, multiplexer_1_out,
       multiplexer_2_out, multiplexer_4_out, ram_1_data, rom_1_data, ula_1_ula_out;

  Register #(.width(16)) register_1 (.D(multiplexer_3_out), .en(in_1), .Q(register_1_q), .clk(CLK), .clr(Clr));
  or or_1 (CLK, clock_1_out, button_1_out);
  Button button_1 (.out(button_1_out));
  Clock clock_1 (.out(clock_1_out));
  Button button_2 (.out(Clr));
  Adder #(.width(16)) adder_1 (.a(16'h1), .b(register_1_q), .out(adder_1_out));  // open: cin, cout
  ROM #(.addrWidth(16), .dataWidth(32)) rom_1 (.addr(register_1_q), .data(rom_1_data), .sel(in_1));
  Adder #(.width(16)) adder_2 (.a(adder_1_out), .b(rom_1_data[15:0]), .out(adder_2_out));  // open: cin, cout
  UC uc_1 (
    .Input(rom_1_data[31:28]), .ULA_Op(uc_1_ula_op), .ULA_Src(uc_1_ula_src), .Jump(uc_1_jump),
    .Branch(uc_1_branch), .Mem2Reg(uc_1_mem2reg), .MemWrite(uc_1_memwrite), .RegWrite(uc_1_regwrite),
    .RegSrc(uc_1_regsrc));
  Multiplexer #(.select(2), .width(32), .enable("false")) multiplexer_1 (
    .in0(multiplexer_4_out), .in1(bit_extender_1_out), .in2(bank_regis_1_rt_out), .out(multiplexer_1_out),
    .sel(uc_1_regsrc));  // open: in3
  not not_1 (not_1_out, CLK);
  assign bit_extender_1_out = {{16{rom_1_data[15]}}, rom_1_data[15:0]};  // Bit_Extender bit_extender_1
  Bank_Regis bank_regis_1 (
    .Clear(Clr), .RD(rom_1_data[27:24]), .WriteValue(multiplexer_1_out), .Write(uc_1_regwrite),
    .RS(rom_1_data[23:20]), .RT(rom_1_data[19:16]), .RS_Out(bank_regis_1_rs_out),
    .RT_Out(bank_regis_1_rt_out), .CLK(not_1_out));
  Multiplexer #(.width(32), .enable("false")) multiplexer_2 (
    .in0(bank_regis_1_rt_out), .in1(bit_extender_1_out), .out(multiplexer_2_out), .sel(uc_1_ula_src));
  Multiplexer #(.width(16), .enable("false")) multiplexer_3 (
    .in0(adder_1_out), .in1(adder_2_out), .out(multiplexer_3_out), .sel(or_2_out));
  or or_2 (or_2_out, uc_1_jump, and_1_out);
  and and_1 (and_1_out, uc_1_branch, ula_1_comp_eq);
  ULA ula_1 (
    .RS(bank_regis_1_rs_out), .RT(multiplexer_2_out), .ULA_Out(ula_1_ula_out), .Comp_EQ(ula_1_comp_eq),
    .OP(uc_1_ula_op));
  Bit_Extender #(.in_width(32), .\type ("sign")) bit_extender_2 (.in(ula_1_ula_out), .out(bit_extender_2_out));
  not not_2 (not_2_out, CLK);
  Multiplexer #(.width(32), .enable("false")) multiplexer_4 (
    .in0(ula_1_ula_out), .in1(ram_1_data), .out(multiplexer_4_out), .sel(uc_1_mem2reg));
  RAM #(.addrWidth(16), .dataWidth(32), .bus("separate")) ram_1 (
    .addr(bit_extender_2_out), .din(bank_regis_1_rt_out), .data(ram_1_data), .str(uc_1_memwrite), .sel(in_1),
    .clk(not_2_out), .ld(uc_1_mem2reg), .clr(Clr));

  // Other names for the same wires on the sheet: On = in_1

  // Notes on the sheet:
  //   contents of rom_1 (hex, n*v repeats v):
  //   0 a1000002 a2000003 930f0000 54120000 1ff40000 a4000003 a5000003 960f0000 57450000 1ff70000 970f0000
  //   58150000 1ff80000 a8000001 a9000000 8091000b aa000000 80a20007 5b920000 1bba0000 1bb30000 c0b80000
  //   28800001 2aa00001 7000fff8 29900001 7000fff4 a8000001 a9000000 8094000b aa000000 80a50007 5b950000
  //   1bba0000 1bb60000 c0b80000 28800001 2aa00001 7000fff8 29900001 7000fff4 a8000000 80810019 a9000000
  //   80950015 aa000000 ab000000 80b2000c 5c820000 1ccb0000 1cc30000 bcc00000 5db50000 1dd90000 1dd60000
  //   bdd00000 5ccd0000 1aac0000 2bb00001 7000fff3 5c850000 1cc90000 1cc70000 c0ca0000 29900001 7000ffea
  //   28800001 7000ffe6
endmodule

module Bank_Regis (
  input  Write,
  input  [3:0] RD,
  input  [3:0] RS,
  input  [3:0] RT,
  input  [31:0] WriteValue,
  input  CLK,
  input  Clear,
  output [31:0] RS_Out,
  output [31:0] RT_Out
);

  wire demultiplexer_1_out0, demultiplexer_1_out1, demultiplexer_1_out2, demultiplexer_1_out3,
       demultiplexer_1_out4, demultiplexer_1_out5, demultiplexer_1_out6, demultiplexer_1_out7,
       demultiplexer_1_out8, demultiplexer_1_out9, demultiplexer_1_out10, demultiplexer_1_out11,
       demultiplexer_1_out12, demultiplexer_1_out13, demultiplexer_1_out14, demultiplexer_1_out15;
  wire [31:0] register_1_q, register_2_q, register_3_q, register_4_q, register_5_q, register_6_q,
       register_7_q, register_8_q, register_9_q, register_10_q, register_11_q, register_12_q, register_13_q,
       register_14_q, register_15_q, register_16_q;

  Demultiplexer #(.select(4), .enable("false")) demultiplexer_1 (
    .out0(demultiplexer_1_out0), .out1(demultiplexer_1_out1), .out2(demultiplexer_1_out2),
    .out3(demultiplexer_1_out3), .out4(demultiplexer_1_out4), .out5(demultiplexer_1_out5),
    .out6(demultiplexer_1_out6), .out7(demultiplexer_1_out7), .out8(demultiplexer_1_out8),
    .out9(demultiplexer_1_out9), .out10(demultiplexer_1_out10), .out11(demultiplexer_1_out11),
    .out12(demultiplexer_1_out12), .out13(demultiplexer_1_out13), .out14(demultiplexer_1_out14),
    .out15(demultiplexer_1_out15), .in(Write), .sel(RD));
  Register #(.width(32)) register_1 (
    .D(WriteValue), .en(demultiplexer_1_out0), .Q(register_1_q), .clk(CLK), .clr(Clear));
  Register #(.width(32)) register_2 (
    .D(WriteValue), .en(demultiplexer_1_out1), .Q(register_2_q), .clk(CLK), .clr(Clear));
  Register #(.width(32)) register_3 (
    .D(WriteValue), .en(demultiplexer_1_out2), .Q(register_3_q), .clk(CLK), .clr(Clear));
  Register #(.width(32)) register_4 (
    .D(WriteValue), .en(demultiplexer_1_out3), .Q(register_4_q), .clk(CLK), .clr(Clear));
  Register #(.width(32)) register_5 (
    .D(WriteValue), .en(demultiplexer_1_out4), .Q(register_5_q), .clk(CLK), .clr(Clear));
  Register #(.width(32)) register_6 (
    .D(WriteValue), .en(demultiplexer_1_out5), .Q(register_6_q), .clk(CLK), .clr(Clear));
  Register #(.width(32)) register_7 (
    .D(WriteValue), .en(demultiplexer_1_out6), .Q(register_7_q), .clk(CLK), .clr(Clear));
  Register #(.width(32)) register_8 (
    .D(WriteValue), .en(demultiplexer_1_out7), .Q(register_8_q), .clk(CLK), .clr(Clear));
  Register #(.width(32)) register_9 (
    .D(WriteValue), .en(demultiplexer_1_out8), .Q(register_9_q), .clk(CLK), .clr(Clear));
  Register #(.width(32)) register_10 (
    .D(WriteValue), .en(demultiplexer_1_out9), .Q(register_10_q), .clk(CLK), .clr(Clear));
  Register #(.width(32)) register_11 (
    .D(WriteValue), .en(demultiplexer_1_out10), .Q(register_11_q), .clk(CLK), .clr(Clear));
  Register #(.width(32)) register_12 (
    .D(WriteValue), .en(demultiplexer_1_out11), .Q(register_12_q), .clk(CLK), .clr(Clear));
  Register #(.width(32)) register_13 (
    .D(WriteValue), .en(demultiplexer_1_out12), .Q(register_13_q), .clk(CLK), .clr(Clear));
  Register #(.width(32)) register_14 (
    .D(WriteValue), .en(demultiplexer_1_out13), .Q(register_14_q), .clk(CLK), .clr(Clear));
  Register #(.width(32)) register_15 (
    .D(WriteValue), .en(demultiplexer_1_out14), .Q(register_15_q), .clk(CLK), .clr(Clear));
  Register #(.width(32)) register_16 (
    .D(WriteValue), .en(demultiplexer_1_out15), .Q(register_16_q), .clk(CLK), .clr(Clear));
  Multiplexer #(.select(4), .width(32), .enable("false")) multiplexer_1 (
    .in0(register_1_q), .in1(register_2_q), .in2(register_3_q), .in3(register_4_q), .in4(register_5_q),
    .in5(register_6_q), .in6(register_7_q), .in7(register_8_q), .in8(register_9_q), .in9(register_10_q),
    .in10(register_11_q), .in11(register_12_q), .in12(register_13_q), .in13(register_14_q),
    .in14(register_15_q), .in15(register_16_q), .out(RS_Out), .sel(RS));
  Multiplexer #(.select(4), .width(32), .enable("false")) multiplexer_2 (
    .in0(register_1_q), .in1(register_2_q), .in2(register_3_q), .in3(register_4_q), .in4(register_5_q),
    .in5(register_6_q), .in6(register_7_q), .in7(register_8_q), .in8(register_9_q), .in9(register_10_q),
    .in10(register_11_q), .in11(register_12_q), .in12(register_13_q), .in13(register_14_q),
    .in14(register_15_q), .in15(register_16_q), .out(RT_Out), .sel(RT));

  // Other names for the same wires on the sheet: Clr = Clear
endmodule

module ULA (
  input  [31:0] RS,
  input  [1:0] OP,
  input  [31:0] RT,
  output [31:0] ULA_Out,
  output Comp_EQ
);

  wire [31:0] adder_1_out, multiplier_1_out, subtractor_1_out;

  Adder #(.width(32)) adder_1 (.a(RS), .b(RT), .out(adder_1_out));  // open: cin, cout
  Subtractor #(.width(32)) subtractor_1 (.a(RS), .b(RT), .out(subtractor_1_out));  // open: bin, bout
  Multiplier #(.width(32)) multiplier_1 (.a(RS), .b(RT), .out(multiplier_1_out));  // open: cin, cout
  Comparator #(.width(32)) comparator_1 (.a(RS), .b(RT), .eq(Comp_EQ));  // open: gt, lt
  Multiplexer #(.select(2), .width(32), .enable("false")) multiplexer_1 (
    .in0(adder_1_out), .in1(subtractor_1_out), .in2(multiplier_1_out), .out(ULA_Out), .sel(OP));  // open: in3
endmodule

module UC (
  input  [3:0] Input,
  output [1:0] ULA_Op,
  output ULA_Src,
  output Jump,
  output Branch,
  output Mem2Reg,
  output MemWrite,
  output RegWrite,
  output [1:0] RegSrc
);

  wire and_4_out, and_5_out, and_6_out, and_7_out, and_8_out, and_9_out, and_10_out, and_12_out, and_13_out,
       and_14_out, not_1_out, not_2_out, not_3_out, not_4_out, not_5_out, not_6_out, not_7_out, not_8_out,
       not_9_out, not_10_out, not_11_out, not_12_out, not_13_out, not_14_out, not_15_out, not_16_out,
       not_17_out, not_18_out, not_19_out;

  not not_1 (not_1_out, Input[1]);
  not not_2 (not_2_out, Input[0]);
  not not_3 (not_3_out, Input[3]);
  not not_4 (not_4_out, Input[2]);
  not not_5 (not_5_out, Input[3]);
  not not_6 (not_6_out, Input[1]);
  not not_7 (not_7_out, Input[0]);
  not not_8 (not_8_out, Input[3]);
  not not_9 (not_9_out, Input[0]);
  not not_10 (not_10_out, Input[0]);
  and and_1 (Jump, Input[2], Input[1], Input[0]);
  not not_11 (not_11_out, Input[2]);
  not not_12 (not_12_out, Input[1]);
  not not_13 (not_13_out, Input[0]);
  and and_2 (Mem2Reg, Input[3], Input[1], Input[0]);
  and and_3 (MemWrite, Input[3], Input[2]);
  not not_14 (not_14_out, Input[1]);
  not not_15 (not_15_out, Input[2]);
  not not_16 (not_16_out, Input[3]);
  not not_17 (not_17_out, Input[0]);
  not not_18 (not_18_out, Input[1]);
  not not_19 (not_19_out, Input[0]);
  and and_4 (and_4_out, Input[2], not_1_out, Input[0]);
  and and_5 (and_5_out, Input[2], Input[1], not_2_out);
  and and_6 (and_6_out, not_3_out, not_4_out, Input[1], Input[0]);
  and and_7 (and_7_out, not_5_out, Input[2], not_6_out, not_7_out);
  and and_8 (and_8_out, not_8_out, Input[1], not_9_out);
  and and_9 (and_9_out, Input[2], not_10_out);
  and and_10 (and_10_out, Input[3], Input[1], Input[0]);
  and and_11 (Branch, Input[3], not_11_out, not_12_out, not_13_out);
  and and_12 (and_12_out, not_14_out, Input[0]);
  and and_13 (and_13_out, not_15_out, Input[1]);
  and and_14 (and_14_out, not_16_out, Input[2], not_17_out);
  and and_15 (RegSrc[1], Input[3], not_18_out, Input[0]);
  and and_16 (RegSrc[0], Input[3], Input[1], not_19_out);
  or or_1 (ULA_Op[1], and_4_out, and_5_out);
  or or_2 (ULA_Op[0], and_6_out, and_7_out);
  or or_3 (ULA_Src, and_8_out, and_9_out, and_10_out);
  or or_4 (RegWrite, and_12_out, and_13_out, and_14_out);
endmodule

module UC2 (
  input  [3:0] Input,
  output [1:0] ULA_Op,
  output ULA_Src,
  output Jump,
  output Branch,
  output Mem2Reg,
  output MemWrite,
  output RegWrite
);

  wire and_1_out, and_2_out, and_3_out, and_4_out, and_5_out, and_6_out, and_7_out, and_8_out, and_9_out,
       and_10_out, and_14_out, and_15_out, and_16_out, not_1_out, not_2_out, not_3_out, not_4_out, not_5_out,
       not_6_out, not_7_out, not_8_out, not_9_out, not_10_out, not_11_out, not_12_out, not_13_out;

  not not_1 (not_1_out, Input[1]);
  and and_1 (and_1_out, Input[2], not_1_out, Input[0]);
  and and_2 (and_2_out, Input[2], Input[1], not_2_out);
  not not_2 (not_2_out, Input[0]);
  and and_3 (and_3_out, Input[3], Input[1], Input[0]);
  not not_3 (not_3_out, Input[2]);
  and and_4 (and_4_out, not_3_out, Input[1], Input[0]);
  and and_5 (and_5_out, Input[2], not_4_out, not_5_out);
  not not_4 (not_4_out, Input[1]);
  not not_5 (not_5_out, Input[0]);
  and and_6 (and_6_out, Input[1], not_6_out);
  not not_6 (not_6_out, Input[0]);
  and and_7 (and_7_out, Input[2], not_7_out);
  not not_7 (not_7_out, Input[0]);
  and and_8 (and_8_out, Input[3], Input[0]);
  and and_9 (and_9_out, Input[2], Input[1], Input[0]);
  and and_10 (and_10_out, Input[3], Input[1], Input[0]);
  and and_11 (Branch, Input[3], not_8_out, not_9_out);
  not not_8 (not_8_out, Input[1]);
  not not_9 (not_9_out, Input[0]);
  and and_12 (Mem2Reg, Input[3], Input[0]);
  and and_13 (MemWrite, Input[3], Input[1]);
  not not_10 (not_10_out, Input[2]);
  and and_14 (and_14_out, not_10_out, Input[0]);
  not not_11 (not_11_out, Input[3]);
  and and_15 (and_15_out, not_11_out, Input[1], not_12_out);
  not not_12 (not_12_out, Input[0]);
  and and_16 (and_16_out, Input[2], not_13_out);
  not not_13 (not_13_out, Input[1]);
  or or_1 (ULA_Op[1], and_1_out, and_2_out, and_3_out);
  or or_2 (ULA_Op[0], and_4_out, and_5_out);
  or or_3 (ULA_Src, and_6_out, and_7_out, and_8_out);
  or or_4 (Jump, and_9_out, and_10_out);
  or or_5 (RegWrite, and_14_out, and_15_out, and_16_out);
endmodule
